// Logisim project proyectoFinal.circ as structural Verilog: 1 circuit, main circuit main
module main (
  input  in_1,
  input  piso
);

  wire e1, e2, e3, e4, e5, e6, e7, e8, e9, e10, e11, e12, e13, e14, e15, e16, mn, rj;
  wire [31:0] t3;
  wire [31:31] t1;

  Clock clock_1 (.out(rj));
  not not_1 (mn, in_1);
  not not_2 (t1[31], piso);
  D_Flip_Flop d_ff_1 (.clk(rj), .D(e16), .Q(e1));  // open: Qn, preset, en, reset
  D_Flip_Flop d_ff_2 (.clk(rj), .D(e8), .Q(e9));  // open: Qn, preset, en, reset
  D_Flip_Flop d_ff_3 (.clk(rj), .D(e1), .Q(e2));  // open: Qn, preset, en, reset
  D_Flip_Flop d_ff_4 (.clk(rj), .D(e9), .Q(e10));  // open: Qn, preset, en, reset
  D_Flip_Flop d_ff_5 (.clk(rj), .D(e2), .Q(e3));  // open: Qn, preset, en, reset
  D_Flip_Flop d_ff_6 (.clk(rj), .D(e10), .Q(e11));  // open: Qn, preset, en, reset
  D_Flip_Flop d_ff_7 (.clk(rj), .D(e3), .Q(e4));  // open: Qn, preset, en, reset
  D_Flip_Flop d_ff_8 (.clk(rj), .D(e11), .Q(e12));  // open: Qn, preset, en, reset
  D_Flip_Flop d_ff_9 (.clk(rj), .D(e4), .Q(e5));  // open: Qn, preset, en, reset
  D_Flip_Flop d_ff_10 (.clk(rj), .D(e12), .Q(e13));  // open: Qn, preset, en, reset
  DotMatrix #(.inputtype("row"), .matrixcols(32), .matrixrows(16)) dotmatrix_1 (
    .row13({t3[31], {2{mn}}, t3[28:0]}),
    .row14({e16, {2{mn}}, e13, e12, e11, e10, e9, e8, e7, e6, e5, e4, e3, e2, e1, e16, e15, e14, e13, e12, e11, e10, e9, e8, e7, e6, e5, e4, e3, e2, e1}),
    .row15({32{t1[31]}}));  // open: row0, row1, row2, row3, row4, row5, row6, row7, row8, row9, row10, row11, row12
  D_Flip_Flop d_ff_11 (.clk(rj), .D(e5), .Q(e6));  // open: Qn, preset, en, reset
  D_Flip_Flop d_ff_12 (.clk(rj), .D(e13), .Q(e14));  // open: Qn, preset, en, reset
  D_Flip_Flop d_ff_13 (.clk(rj), .D(e6), .Q(e7));  // open: Qn, preset, en, reset
  D_Flip_Flop d_ff_14 (.clk(rj), .D(e14), .Q(e15));  // open: Qn, preset, en, reset
  D_Flip_Flop d_ff_15 (.clk(rj), .D(e7), .Q(e8));  // open: Qn, preset, en, reset
  D_Flip_Flop d_ff_16 (.clk(rj), .D(e15), .Q(e16));  // open: Qn, preset, en, reset

  // Other names for the same wires on the sheet: t1[30:0] = {31{t1[31]}};
  //   t2[31:0] = {e16, {2{mn}}, e13, e12, e11, e10, e9, e8, e7, e6, e5, e4, e3, e2, e1, e16, e15, e14, e13, e12, e11, e10, e9, e8, e7, e6, e5, e4, e3, e2, e1};
  //   t3[30:29] = {2{mn}}

  // Notes on the sheet:
  //   jugador
endmodule
